# Fritzing sketch odometry-design-ROS-Blocks (saved by Fritzing 0.9.3b)
breadboards: 1

parts:
  WeMos_D1_Mini1 = WeMos D1 Mini
  GY1 = MPU-6050 Board GY-521 [form="♀ (female)" package=THT]  # not connected
  Part1 = SRF05 Ultrasonic Rangefinder
  U1 = ADNS2610 [package=adns2610]
  U2 = ADNS2610 [package=adns2610]

nets:
  N1: WeMos_D1_Mini1.D1, U2.SDIO
  N2: WeMos_D1_Mini1.D2, U2.OSC_OUT
  N3: WeMos_D1_Mini1.D3, U1.SDIO
  N4: WeMos_D1_Mini1.D4, U1.OSC_OUT
  N5: Part1.VCC, U1.OSC_IN, U2.OSC_IN
  N6: U1.SCK, U2.SCK

notes:
  PS2 mouse sensor is only indecative here.

custom parts:
  MPU-6050 Board GY-521: Acelerometro y Giroscopio MPU-6050 Board GY-521
